// Logisim project CPU.circ as structural Verilog: 12 circuits, main circuit ALU
module Main (
);

  wire ALU_branch_signal, and_1_out, CLK, clock_1_out, control_logic_2_main_1_regdst, HALT, or_1_out, RESET,
       RRead, RWrite;
  wire [1:0] control_logic_2_main_1_memtoreg;
  wire [2:0] ALU_Control_out_3, control_logic_2_main_1_aluop, multiplexer_4_out;
  wire [2:2] control_logic_2_main_1_regwrite;
  wire [3:0] control_logic_2_main_1_memread;
  wire [6:0] control_logic_2_main_1_alusrc;
  wire [15:0] adder_1_out, adder_2_out, ALU_max, ALU_min, ALU_out_6, bit_extender_1_out, multiplexer_1_out,
       multiplexer_3_out, multiplexer_5_out, multiplexer_6_out, multiplexer_7_out, multiplexer_8_out, PC_q,
       RA_Register_data_1, ram_1_data, Register_data_1, Register_data_2, rom_1_data, subtractor_1_out;

  Button button_1 (.out(RESET));
  Multiplexer #(.width(16), .enable("false")) multiplexer_1 (
    .in0(multiplexer_3_out), .in1(multiplexer_5_out), .out(multiplexer_1_out), .sel(RRead));
  Clock clock_1 (.out(clock_1_out));
  Multiplexer #(.enable("false")) multiplexer_2 (.in0(clock_1_out), .in1(1'b0), .out(CLK), .sel(HALT));
  Register_part #(.width(16)) PC (.D(adder_1_out), .Q(PC_q), .clk(CLK), .clr(RESET));  // open: en
  Subtract_64 Subtract64 (.in_1(multiplexer_1_out));  // open: out_2
  Multiplexer #(.width(16), .enable("false")) multiplexer_3 (
    .in0(adder_1_out), .in1(adder_2_out), .out(multiplexer_3_out), .sel(or_1_out));
  Adder #(.width(16)) adder_1 (.a(PC_q), .b(16'h1), .out(adder_1_out));  // open: cin, cout
  ROM #(.addrWidth(16), .dataWidth(16)) rom_1 (.addr(PC_q), .data(rom_1_data));  // open: sel
  RA_Register RA_Register (
    .Write(RWrite), .in_2(adder_1_out), .CLK(CLK), .RESET(RESET), .Read(RRead), .Data_1(RA_Register_data_1));
  Control_logic_2_main control_logic_2_main_1 (
    .opcode(rom_1_data[3:0]), .RegDst(control_logic_2_main_1_regdst),
    .ALUSrc(control_logic_2_main_1_alusrc[0]), .MemtoReg(control_logic_2_main_1_memtoreg),
    .RegWrite(control_logic_2_main_1_regwrite[2]), .MemRead(control_logic_2_main_1_memread[0]),
    .MemWrite(control_logic_2_main_1_memread[1]), .Branch(control_logic_2_main_1_memread[2]),
    .Jump(control_logic_2_main_1_memread[3]), .ALUOp(control_logic_2_main_1_aluop), .RA_Read(RRead),
    .RA_Write(RWrite), .HALT(HALT), .li(control_logic_2_main_1_alusrc[6]));
  assign bit_extender_1_out = {{10{1'b0}}, rom_1_data[15:10]};  // Bit_Extender bit_extender_1
  // Probe on rom_1_data[9:7]
  // Probe on rom_1_data[12:10]
  Multiplexer #(.width(3), .enable("false")) multiplexer_4 (
    .in0(rom_1_data[6:4]), .in1(rom_1_data[12:10]), .out(multiplexer_4_out),
    .sel(control_logic_2_main_1_regdst));
  Multiplexer #(.width(16), .enable("false")) multiplexer_5 (
    .in0({16{1'b0}}), .in1(RA_Register_data_1), .out(multiplexer_5_out), .sel(RRead));
  // Probe on multiplexer_4_out
  // Probe on bit_extender_1_out
  // Probe on Register_data_1
  Register Register (
    .Write(control_logic_2_main_1_regwrite[2]), .Write_Register(multiplexer_4_out),
    .Register_Data(multiplexer_8_out), .CLK(CLK), .Data_1(Register_data_1), .Data_2(Register_data_2),
    .RESET(RESET), .Read_Register_2(rom_1_data[9:7]), .Read_Register_1(rom_1_data[12:10]));
  // Probe on Register_data_2
  // Probe on multiplexer_6_out
  and and_1 (and_1_out, control_logic_2_main_1_memread[2], ALU_branch_signal);
  Multiplexer #(.width(16), .enable("false")) multiplexer_6 (
    .in0(Register_data_2), .in1(bit_extender_1_out), .out(multiplexer_6_out),
    .sel(control_logic_2_main_1_alusrc[0]));
  ALU_Control ALU_Control (
    .Funct(bit_extender_1_out[2:0]), .ALUOp(control_logic_2_main_1_aluop), .out_3(ALU_Control_out_3));
  or or_1 (or_1_out, and_1_out, control_logic_2_main_1_memread[3]);
  Multiplexer #(.width(16), .enable("false")) multiplexer_7 (
    .in0(Register_data_1), .in1({16{1'b0}}), .out(multiplexer_7_out), .sel(control_logic_2_main_1_alusrc[6]));
  // Probe on multiplexer_7_out
  Adder #(.width(16)) adder_2 (.a(adder_1_out), .b(subtractor_1_out), .out(adder_2_out));  // open: cin, cout
  Subtractor #(.width(16)) subtractor_1 (.a(bit_extender_1_out), .b(16'h1), .out(subtractor_1_out));  // open: bin, bout
  ALU ALU (
    .Data_1(multiplexer_7_out), .Data_2(multiplexer_6_out), .Branch_Signal(ALU_branch_signal),
    .out_6(ALU_out_6), .ALU_Signal(ALU_Control_out_3), .Max(ALU_max), .Min(ALU_min));
  // Probe on ALU_out_6
  RAM #(.addrWidth(16), .dataWidth(16), .bus("separate")) ram_1 (
    .addr(ALU_out_6), .din(Register_data_2), .data(ram_1_data), .str(control_logic_2_main_1_memread[1]),
    .clk(CLK), .ld(control_logic_2_main_1_memread[0]), .clr(RESET));  // open: sel
  // Probe on multiplexer_8_out
  Multiplexer #(.select(2), .width(16), .enable("false")) multiplexer_8 (
    .in0(ALU_out_6), .in1(ram_1_data), .in2(ALU_max), .in3(ALU_min), .out(multiplexer_8_out),
    .sel(control_logic_2_main_1_memtoreg));

  // Notes on the sheet:
  //   contents of rom_1 (hex, n*v repeats v):
  //   400 810 2820 411 fcaa f 12*0 1
endmodule

module ALU (
  input  [15:0] Data_1,
  input  [15:0] Data_2,
  input  [2:0] ALU_Signal,
  output [15:0] Max,
  output [15:0] Min,
  output [15:0] out_6,
  output Branch_Signal
);

  wire and_2_out, and_3_out, comparator_1_eq, comparator_2_gt, comparator_2_lt, comparator_3_lt, not_1_out;
  wire [15:0] adder_1_out, and_1_out, or_1_out, shifter_1_out, shifter_2_out, shifter_3_out;

  Multiplexer #(.width(16), .enable("false")) multiplexer_1 (
    .in0(Data_1), .in1(Data_2), .out(Max), .sel(comparator_2_lt));
  Multiplexer #(.width(16), .enable("false")) multiplexer_2 (
    .in0(Data_1), .in1(Data_2), .out(Min), .sel(comparator_2_gt));
  Comparator #(.width(16)) comparator_1 (.a(Data_1), .b(Data_2), .eq(comparator_1_eq));  // open: gt, lt
  not not_1 (not_1_out, comparator_1_eq);
  Comparator #(.width(16), .mode("unsigned")) comparator_2 (
    .a(Data_1), .b(Data_2), .gt(comparator_2_gt), .lt(comparator_2_lt));  // open: eq
  Adder #(.width(16)) adder_1 (.a(Data_1), .b(Data_2), .out(adder_1_out));  // open: cin, cout
  assign and_1_out = Data_1 & Data_2;  // AND_Gate and_1, 16 bits wide
  assign or_1_out = Data_1 | Data_2;  // OR_Gate or_1, 16 bits wide
  Shifter #(.width(16)) shifter_1 (.in(Data_1), .\dist (Data_2[3:0]), .out(shifter_1_out));
  Shifter #(.width(16), .shift("lr")) shifter_2 (.in(Data_1), .\dist (Data_2[3:0]), .out(shifter_2_out));
  Shifter #(.width(16), .shift("ar")) shifter_3 (.in(Data_1), .\dist (Data_2[3:0]), .out(shifter_3_out));
  Comparator #(.width(16)) comparator_3 (.a(Data_1), .b(Data_2), .lt(comparator_3_lt));  // open: gt, eq
  and and_2 (and_2_out, not_1_out, ALU_Signal[0], ALU_Signal[1], ALU_Signal[2]);
  Multiplexer #(.select(3), .width(16)) multiplexer_3 (
    .in0(adder_1_out), .in1(and_1_out), .in2(or_1_out), .in4(shifter_1_out), .in5(shifter_2_out),
    .in6(shifter_3_out), .out(out_6), .sel(ALU_Signal), .en(1'b1));  // open: in3, in7
  and and_3 (and_3_out, comparator_3_lt, ~ALU_Signal[0], ALU_Signal[1], ALU_Signal[2]);  // AND_Gate
  or or_2 (Branch_Signal, and_3_out, and_2_out);
endmodule

module ALU_Control (
  input  [2:0] Funct,
  input  [2:0] ALUOp,
  output [2:0] out_3
);

  wire comparator_1_eq;
  wire [2:0] subtractor_1_out;

  Subtractor #(.width(3)) subtractor_1 (.a(ALUOp), .b(3'b001), .out(subtractor_1_out));  // open: bin, bout
  // Probe on subtractor_1_out
  Comparator #(.width(3)) comparator_1 (.a(ALUOp), .b(3'b000), .eq(comparator_1_eq));  // open: gt, lt
  Multiplexer #(.width(3), .enable("false")) multiplexer_1 (
    .in0(subtractor_1_out), .in1(Funct), .out(out_3), .sel(comparator_1_eq));
endmodule

module Register (
  input  Write,
  input  [2:0] Write_Register,
  input  [15:0] Register_Data,
  input  [2:0] Read_Register_2,
  input  [2:0] Read_Register_1,
  input  CLK,
  input  RESET,
  output [15:0] Data_1,
  output [15:0] Data_2
);

  wire and_1_out, and_2_out, and_3_out, and_4_out, and_5_out, and_6_out, and_7_out, and_8_out,
       decoder_1_out0, decoder_1_out1, decoder_1_out2, decoder_1_out3, decoder_1_out4, decoder_1_out5,
       decoder_1_out6, decoder_1_out7;
  wire [15:0] register_1_q, register_2_q, register_3_q, register_4_q, register_5_q, register_6_q,
       register_7_q, register_8_q;

  Decoder #(.select(3), .enable("false")) decoder_1 (
    .out0(decoder_1_out0), .out1(decoder_1_out1), .out2(decoder_1_out2), .out3(decoder_1_out3),
    .out4(decoder_1_out4), .out5(decoder_1_out5), .out6(decoder_1_out6), .out7(decoder_1_out7),
    .sel(Write_Register));
  and and_1 (and_1_out, Write, decoder_1_out0);
  and and_2 (and_2_out, Write, decoder_1_out1);
  and and_3 (and_3_out, Write, decoder_1_out2);
  and and_4 (and_4_out, Write, decoder_1_out3);
  and and_5 (and_5_out, Write, decoder_1_out4);
  and and_6 (and_6_out, Write, decoder_1_out5);
  and and_7 (and_7_out, Write, decoder_1_out6);
  and and_8 (and_8_out, Write, decoder_1_out7);
  Register_part #(.width(16)) register_1 (.D(Register_Data), .en(and_1_out), .Q(register_1_q), .clk(CLK), .clr(RESET));
  Register_part #(.width(16)) register_2 (.D(Register_Data), .en(and_2_out), .Q(register_2_q), .clk(CLK), .clr(RESET));
  Register_part #(.width(16)) register_3 (.D(Register_Data), .en(and_3_out), .Q(register_3_q), .clk(CLK), .clr(RESET));
  Register_part #(.width(16)) register_4 (.D(Register_Data), .en(and_4_out), .Q(register_4_q), .clk(CLK), .clr(RESET));
  Register_part #(.width(16)) register_5 (.D(Register_Data), .en(and_5_out), .Q(register_5_q), .clk(CLK), .clr(RESET));
  Register_part #(.width(16)) register_6 (.D(Register_Data), .en(and_6_out), .Q(register_6_q), .clk(CLK), .clr(RESET));
  Register_part #(.width(16)) register_7 (.D(Register_Data), .en(and_7_out), .Q(register_7_q), .clk(CLK), .clr(RESET));
  Register_part #(.width(16)) register_8 (.D(Register_Data), .en(and_8_out), .Q(register_8_q), .clk(CLK), .clr(RESET));
  Multiplexer #(.select(3), .width(16), .enable("false")) multiplexer_1 (
    .in0(register_1_q), .in1(register_2_q), .in2(register_3_q), .in3(register_4_q), .in4(register_5_q),
    .in5(register_6_q), .in6(register_7_q), .in7(register_8_q), .out(Data_1), .sel(Read_Register_1));
  Multiplexer #(.select(3), .width(16), .enable("false")) multiplexer_2 (
    .in0(register_1_q), .in1(register_2_q), .in2(register_3_q), .in3(register_4_q), .in4(register_5_q),
    .in5(register_6_q), .in6(register_7_q), .in7(register_8_q), .out(Data_2), .sel(Read_Register_2));
endmodule

module RA_Control (
  input  a,
  input  b,
  input  c,
  input  d,
  output RARead,
  output RAWrite
);

  wire not_1_out, not_2_out;

  not not_1 (not_1_out, d);
  not not_2 (not_2_out, c);
  and and_1 (RARead, a, b, c, not_1_out);
  and and_2 (RAWrite, a, b, not_2_out, d);
endmodule

module Control_12_pin (
  input  a,
  input  b,
  input  c,
  input  d,
  output RegDst,
  output ALUSrc,
  output MemtoReg1,
  output MemtoReg0,
  output RegWrite,
  output MemRead,
  output MemWrite,
  output Branch,
  output Jump,
  output ALUOp2,
  output ALUOp1,
  output ALUOp0
);

  wire and_1_out, and_2_out, and_3_out, and_4_out, and_5_out, and_6_out, and_7_out, and_8_out, and_9_out,
       and_11_out, and_12_out, and_13_out, and_14_out, and_15_out, and_16_out, and_17_out, and_21_out,
       and_22_out, and_24_out, and_25_out, and_26_out, and_27_out, not_1_out, not_2_out, not_3_out,
       not_4_out, not_5_out, not_6_out, not_7_out, not_8_out, not_9_out, not_10_out, not_11_out, not_12_out,
       not_13_out, not_14_out, not_15_out, not_16_out, not_17_out, not_18_out, not_19_out, not_20_out,
       not_21_out, not_22_out, not_23_out, not_24_out, not_25_out, not_26_out, not_27_out, not_28_out,
       not_29_out, not_30_out, not_31_out, not_32_out, not_33_out, not_34_out, not_35_out, not_36_out,
       not_37_out, not_38_out, not_39_out, not_40_out, not_41_out, not_42_out, not_43_out, not_44_out,
       not_45_out, not_46_out, not_47_out, not_48_out, not_49_out, not_50_out, not_51_out, not_52_out,
       not_53_out;

  not not_1 (not_1_out, a);
  not not_2 (not_2_out, b);
  not not_3 (not_3_out, c);
  not not_4 (not_4_out, d);
  not not_5 (not_5_out, a);
  not not_6 (not_6_out, c);
  not not_7 (not_7_out, a);
  not not_8 (not_8_out, d);
  not not_9 (not_9_out, a);
  and and_1 (and_1_out, not_9_out, not_10_out, d);
  not not_10 (not_10_out, b);
  not not_11 (not_11_out, a);
  not not_12 (not_12_out, b);
  and and_2 (and_2_out, not_11_out, not_12_out, c);
  and and_3 (and_3_out, a, not_13_out, not_14_out);
  not not_13 (not_13_out, b);
  not not_14 (not_14_out, c);
  and and_4 (and_4_out, a, b, d);
  not not_15 (not_15_out, a);
  not not_16 (not_16_out, c);
  not not_17 (not_17_out, a);
  not not_18 (not_18_out, d);
  not not_19 (not_19_out, a);
  not not_20 (not_20_out, d);
  not not_21 (not_21_out, b);
  not not_22 (not_22_out, c);
  not not_23 (not_23_out, d);
  not not_24 (not_24_out, a);
  and and_5 (and_5_out, not_24_out, not_25_out);
  not not_25 (not_25_out, b);
  not not_26 (not_26_out, a);
  and and_6 (and_6_out, not_26_out, not_27_out);
  not not_27 (not_27_out, c);
  not not_28 (not_28_out, a);
  and and_7 (and_7_out, not_28_out, not_29_out);
  not not_29 (not_29_out, d);
  not not_30 (not_30_out, b);
  and and_8 (and_8_out, not_30_out, not_31_out, not_32_out);
  not not_31 (not_31_out, c);
  not not_32 (not_32_out, d);
  and and_9 (and_9_out, a, b, d);
  not not_33 (not_33_out, b);
  not not_34 (not_34_out, c);
  not not_35 (not_35_out, d);
  not not_36 (not_36_out, b);
  not not_37 (not_37_out, c);
  not not_38 (not_38_out, c);
  not not_39 (not_39_out, d);
  not not_40 (not_40_out, a);
  not not_41 (not_41_out, b);
  not not_42 (not_42_out, a);
  not not_43 (not_43_out, c);
  not not_44 (not_44_out, d);
  not not_45 (not_45_out, a);
  and and_10 (ALUOp1, not_45_out, not_46_out, c);
  not not_46 (not_46_out, b);
  not not_47 (not_47_out, a);
  not not_48 (not_48_out, b);
  not not_49 (not_49_out, a);
  not not_50 (not_50_out, c);
  not not_51 (not_51_out, d);
  not not_52 (not_52_out, b);
  not not_53 (not_53_out, c);
  and and_11 (and_11_out, not_1_out, not_2_out, not_3_out, not_4_out);
  and and_12 (and_12_out, not_5_out, b, not_6_out, d);
  or or_1 (RegDst, and_11_out, and_12_out, and_13_out);
  and and_13 (and_13_out, not_7_out, b, c, not_8_out);
  or or_2 (ALUSrc, and_1_out, and_2_out, and_3_out, and_4_out);
  and and_14 (and_14_out, not_15_out, b, not_16_out, d);
  or or_3 (MemtoReg1, and_14_out, and_15_out);
  and and_15 (and_15_out, not_17_out, b, c, not_18_out);
  and and_16 (and_16_out, not_19_out, b, c, not_20_out);
  or or_4 (MemtoReg0, and_16_out, and_17_out);
  and and_17 (and_17_out, a, not_21_out, not_22_out, not_23_out);
  or or_5 (RegWrite, and_5_out, and_6_out, and_7_out, and_8_out, and_9_out);
  and and_18 (MemRead, a, not_33_out, not_34_out, not_35_out);
  and and_19 (MemWrite, a, not_36_out, not_37_out, d);
  and and_20 (Branch, a, b, not_38_out, not_39_out);
  and and_21 (and_21_out, not_40_out, b, c, d);
  or or_6 (Jump, and_21_out, and_22_out);
  and and_22 (and_22_out, a, not_41_out, c);
  and and_23 (ALUOp2, not_42_out, b, not_43_out, not_44_out);
  and and_24 (and_24_out, not_47_out, not_48_out, d);
  and and_25 (and_25_out, not_49_out, b, not_50_out, not_51_out);
  and and_26 (and_26_out, a, not_52_out, not_53_out);
  and and_27 (and_27_out, a, b, d);
  or or_7 (ALUOp0, and_24_out, and_25_out, and_26_out, and_27_out);
endmodule

module Control_Logic (
  input  [3:0] opcode,
  output RegDst,
  output ALUSrc,
  output [1:0] MemtoReg,
  output RegWrite,
  output MemRead,
  output MemWrite,
  output Branch,
  output Jump,
  output [2:0] ALUOp,
  output RA_Read,
  output RA_Write,
  output HALT,
  output li
);

  Control_12_pin control_12_pin_1 (
    .a(opcode[3]), .b(opcode[2]), .c(opcode[1]), .d(opcode[0]), .RegDst(RegDst), .ALUSrc(ALUSrc),
    .MemtoReg1(MemtoReg[1]), .MemtoReg0(MemtoReg[0]), .RegWrite(RegWrite), .MemRead(MemRead),
    .MemWrite(MemWrite), .Branch(Branch), .Jump(Jump), .ALUOp2(ALUOp[2]), .ALUOp1(ALUOp[1]), .ALUOp0(ALUOp[0]));
  RA_Control ra_control_1 (
    .a(opcode[3]), .b(opcode[2]), .c(opcode[1]), .d(opcode[0]), .RARead(RA_Read), .RAWrite(RA_Write));
  Comparator #(.width(4)) comparator_1 (.a(opcode), .b(4'b1111), .eq(HALT));  // open: gt, lt
  Comparator #(.width(4)) comparator_2 (.a(opcode), .b(4'b1101), .eq(li));  // open: gt, lt
endmodule

module RA_Register (
  input  Write,
  input  [15:0] in_2,
  input  Read,
  input  CLK,
  input  RESET,
  output [15:0] Data_1
);

  wire [15:0] register_1_q;

  Register_part #(.width(16)) register_1 (.D(in_2), .en(Write), .Q(register_1_q), .clk(CLK), .clr(RESET));
  assign Data_1 = Read ? register_1_q : 16'bz;  // Controlled_Buffer controlled_buffer_1
endmodule

module Subtract_64 (
  input  [15:0] in_1,
  output [15:0] out_2
);

  wire comparator_1_gt;
  wire [15:0] subtractor_1_out;

  Subtractor #(.width(16)) subtractor_1 (.a(in_1), .b(16'h40), .out(subtractor_1_out));  // open: bin, bout
  Comparator #(.width(16), .mode("unsigned")) comparator_1 (
    .a(in_1), .b(16'h40), .gt(comparator_1_gt));  // open: eq, lt
  Multiplexer #(.width(16), .enable("false")) multiplexer_1 (
    .in0(in_1), .in1(subtractor_1_out), .out(out_2), .sel(comparator_1_gt));
endmodule

module \table  (
  input  a,
  input  b,
  input  c,
  input  d,
  output RegDst,
  output AluSrc,
  output MemToReg1,
  output MemToReg0,
  output RegWrite,
  output MemRead,
  output MemWrite,
  output Branch,
  output Jump,
  output ALUop2,
  output ALUop1,
  output ALUop0
);

  wire and_1_out, and_2_out, and_3_out, and_4_out, and_5_out, and_6_out, and_7_out, and_8_out, and_10_out,
       and_11_out, and_12_out, and_13_out, and_14_out, and_18_out, and_19_out, and_20_out, and_21_out,
       and_22_out, not_1_out, not_2_out, not_3_out, not_4_out, not_5_out, not_6_out, not_7_out, not_8_out,
       not_9_out, not_10_out, not_11_out, not_12_out, not_13_out, not_14_out, not_15_out, not_16_out,
       not_17_out, not_18_out, not_19_out, not_20_out, not_21_out, not_22_out, not_23_out, not_24_out,
       not_25_out, not_26_out, not_27_out, not_28_out, not_29_out, not_30_out, not_31_out, not_32_out,
       not_33_out, not_34_out, not_35_out, not_36_out, not_37_out, not_38_out, not_39_out, not_40_out;

  not not_1 (not_1_out, a);
  not not_2 (not_2_out, b);
  and and_1 (and_1_out, not_1_out, not_2_out, d);
  not not_3 (not_3_out, a);
  and and_2 (and_2_out, not_3_out, not_4_out, c);
  not not_4 (not_4_out, b);
  not not_5 (not_5_out, a);
  not not_6 (not_6_out, c);
  and and_3 (and_3_out, not_5_out, not_6_out, not_7_out);
  not not_7 (not_7_out, d);
  not not_8 (not_8_out, a);
  and and_4 (and_4_out, not_8_out, b);
  and and_5 (and_5_out, a, not_9_out, not_10_out);
  not not_9 (not_9_out, b);
  not not_10 (not_10_out, c);
  not not_11 (not_11_out, a);
  not not_12 (not_12_out, c);
  not not_13 (not_13_out, d);
  not not_14 (not_14_out, a);
  and and_6 (and_6_out, not_14_out, not_15_out);
  not not_15 (not_15_out, d);
  not not_16 (not_16_out, b);
  and and_7 (and_7_out, not_16_out, not_17_out);
  not not_17 (not_17_out, c);
  not not_18 (not_18_out, a);
  and and_8 (and_8_out, not_18_out, c);
  not not_19 (not_19_out, a);
  not not_20 (not_20_out, c);
  not not_21 (not_21_out, d);
  not not_22 (not_22_out, a);
  not not_23 (not_23_out, c);
  and and_9 (Branch, a, not_24_out, c);
  not not_24 (not_24_out, b);
  and and_10 (and_10_out, a, b, not_25_out);
  not not_25 (not_25_out, c);
  and and_11 (and_11_out, a, b, not_26_out);
  not not_26 (not_26_out, d);
  not not_27 (not_27_out, a);
  not not_28 (not_28_out, c);
  not not_29 (not_29_out, d);
  not not_30 (not_30_out, b);
  not not_31 (not_31_out, b);
  and and_12 (and_12_out, not_31_out, c, d);
  and and_13 (and_13_out, a, not_32_out, d);
  not not_32 (not_32_out, b);
  and and_14 (and_14_out, a, not_33_out, c);
  not not_33 (not_33_out, b);
  not not_34 (not_34_out, a);
  not not_35 (not_35_out, b);
  not not_36 (not_36_out, d);
  not not_37 (not_37_out, b);
  not not_38 (not_38_out, c);
  not not_39 (not_39_out, d);
  not not_40 (not_40_out, b);
  or or_1 (RegDst, and_1_out, and_2_out);
  or or_2 (AluSrc, and_3_out, and_4_out, and_5_out);
  and and_15 (MemToReg0, not_11_out, b, not_12_out, not_13_out);
  or or_3 (RegWrite, and_6_out, and_7_out, and_8_out);
  and and_16 (MemRead, not_19_out, b, not_20_out, not_21_out);
  and and_17 (MemWrite, not_22_out, b, not_23_out, d);
  or or_4 (Jump, and_10_out, and_11_out);
  and and_18 (and_18_out, not_27_out, b, not_28_out, not_29_out);
  or or_5 (ALUop2, and_18_out, and_19_out);
  and and_19 (and_19_out, a, not_30_out, c);
  or or_6 (ALUop1, and_12_out, and_13_out, and_14_out);
  and and_20 (and_20_out, not_34_out, not_35_out, c, not_36_out);
  and and_21 (and_21_out, a, not_37_out, not_38_out, not_39_out);
  or or_7 (ALUop0, and_20_out, and_21_out, and_22_out);
  and and_22 (and_22_out, a, not_40_out, c, d);

  assign MemToReg1 = 1'b0;
endmodule

module Control_logic_2_main (
  input  [3:0] opcode,
  output RegDst,
  output ALUSrc,
  output [1:0] MemtoReg,
  output RegWrite,
  output MemRead,
  output MemWrite,
  output Branch,
  output Jump,
  output [2:0] ALUOp,
  output RA_Read,
  output RA_Write,
  output HALT,
  output li
);

  \table  table_1 (
    .a(opcode[3]), .b(opcode[2]), .c(opcode[1]), .d(opcode[0]), .RegDst(RegDst), .AluSrc(ALUSrc),
    .MemToReg1(MemtoReg[1]), .MemToReg0(MemtoReg[0]), .RegWrite(RegWrite), .MemRead(MemRead),
    .MemWrite(MemWrite), .Branch(Branch), .Jump(Jump), .ALUop2(ALUOp[2]), .ALUop1(ALUOp[1]), .ALUop0(ALUOp[0]));
  RA_Control ra_control_1 (
    .a(opcode[3]), .b(opcode[2]), .c(opcode[1]), .d(opcode[0]), .RARead(RA_Read), .RAWrite(RA_Write));
  Comparator #(.width(4)) comparator_1 (.a(opcode), .b(4'b1111), .eq(HALT));  // open: gt, lt
  Comparator #(.width(4)) comparator_2 (.a(opcode), .b(4'b0000), .eq(li));  // open: gt, lt
endmodule

module new_main (
  input  RESET
);

  wire ALU_branch_signal, and_1_out, clock_1_out, control_logic_2_main_1_alusrc, control_logic_2_main_1_halt,
       control_logic_2_main_1_li, control_logic_2_main_1_ra_write, control_logic_2_main_1_regdst,
       multiplexer_3_out, or_1_out;
  wire [1:0] control_logic_2_main_1_memtoreg;
  wire [2:0] control_logic_2_main_1_aluop, multiplexer_4_out;
  wire [2:2] control_logic_2_main_1_regwrite;
  wire [3:0] rom_1_data;
  wire [4:0] control_logic_2_main_1_memread;
  wire [15:0] adder_1_out, adder_2_out, ALU_max, ALU_min, ALU_out_6, bit_extender_1_out, multiplexer_1_out,
       multiplexer_2_out, multiplexer_5_out, multiplexer_6_out, multiplexer_7_out, multiplexer_8_out, PC_q,
       RA_Register_data_1, ram_1_data, Register_data_1, Register_data_2, Subtract64_out_2, subtractor_1_out;
  wire [15:2] rom_1_data_2;

  Clock clock_1 (.out(clock_1_out));
  Multiplexer #(.width(16), .enable("false")) multiplexer_1 (
    .in0(adder_1_out), .in1(adder_2_out), .out(multiplexer_1_out), .sel(or_1_out));
  Multiplexer #(.width(16), .enable("false")) multiplexer_2 (
    .in0(multiplexer_1_out), .in1(multiplexer_5_out), .out(multiplexer_2_out),
    .sel(control_logic_2_main_1_memread[4]));
  Subtract_64 Subtract64 (.in_1(multiplexer_2_out), .out_2(Subtract64_out_2));
  Register_part #(.width(16)) PC (.D(Subtract64_out_2), .Q(PC_q), .clk(multiplexer_3_out), .clr(RESET));  // open: en
  Multiplexer #(.enable("false")) multiplexer_3 (
    .in0(clock_1_out), .in1(1'b0), .out(multiplexer_3_out), .sel(control_logic_2_main_1_halt));
  ROM #(.addrWidth(16), .dataWidth(16)) rom_1 (
    .addr(PC_q), .data({rom_1_data_2[15], rom_1_data[3:2], rom_1_data_2[12:2], rom_1_data[1:0]}));  // open: sel
  Adder #(.width(16)) adder_1 (.a(PC_q), .b(16'h1), .out(adder_1_out));  // open: cin, cout
  Control_logic_2_main control_logic_2_main_1 (
    .opcode(rom_1_data), .RegDst(control_logic_2_main_1_regdst), .ALUSrc(control_logic_2_main_1_alusrc),
    .MemtoReg(control_logic_2_main_1_memtoreg), .RegWrite(control_logic_2_main_1_regwrite[2]),
    .MemRead(control_logic_2_main_1_memread[0]), .MemWrite(control_logic_2_main_1_memread[1]),
    .Branch(control_logic_2_main_1_memread[2]), .Jump(control_logic_2_main_1_memread[3]),
    .ALUOp(control_logic_2_main_1_aluop), .RA_Read(control_logic_2_main_1_memread[4]),
    .RA_Write(control_logic_2_main_1_ra_write), .HALT(control_logic_2_main_1_halt),
    .li(control_logic_2_main_1_li));
  Multiplexer #(.width(3), .enable("false")) multiplexer_4 (
    .in0(rom_1_data_2[12:10]), .in1(rom_1_data_2[6:4]), .out(multiplexer_4_out),
    .sel(control_logic_2_main_1_regdst));
  assign bit_extender_1_out = {{10{1'b0}}, {rom_1_data_2[15], rom_1_data_2[6:2]}};  // Bit_Extender bit_extender_1
  RA_Register RA_Register (
    .Write(control_logic_2_main_1_ra_write), .in_2(adder_1_out), .CLK(multiplexer_3_out), .RESET(RESET),
    .Read(control_logic_2_main_1_memread[4]), .Data_1(RA_Register_data_1));
  Multiplexer #(.width(16), .enable("false")) multiplexer_5 (
    .in0({16{1'b0}}), .in1(RA_Register_data_1), .out(multiplexer_5_out),
    .sel(control_logic_2_main_1_memread[4]));
  Subtractor #(.width(16)) subtractor_1 (.a(bit_extender_1_out), .b(16'h1), .out(subtractor_1_out));  // open: bin, bout
  Register Register (
    .Write(control_logic_2_main_1_regwrite[2]), .Write_Register(multiplexer_4_out),
    .Register_Data(multiplexer_8_out), .CLK(multiplexer_3_out), .Data_1(Register_data_1),
    .Data_2(Register_data_2), .RESET(RESET), .Read_Register_2(rom_1_data_2[12:10]),
    .Read_Register_1(rom_1_data_2[9:7]));
  Multiplexer #(.width(16), .enable("false")) multiplexer_6 (
    .in0(Register_data_2), .in1(bit_extender_1_out), .out(multiplexer_6_out),
    .sel(control_logic_2_main_1_alusrc));
  Multiplexer #(.width(16), .enable("false")) multiplexer_7 (
    .in0(Register_data_1), .in1({16{1'b0}}), .out(multiplexer_7_out), .sel(control_logic_2_main_1_li));
  Adder #(.width(16)) adder_2 (.a(adder_1_out), .b(subtractor_1_out), .out(adder_2_out));  // open: cin, cout
  ALU ALU (
    .Data_1(multiplexer_7_out), .Data_2(multiplexer_6_out), .Branch_Signal(ALU_branch_signal),
    .out_6(ALU_out_6), .ALU_Signal(control_logic_2_main_1_aluop), .Max(ALU_max), .Min(ALU_min));
  and and_1 (and_1_out, control_logic_2_main_1_memread[2], ALU_branch_signal);
  or or_1 (or_1_out, and_1_out, control_logic_2_main_1_memread[3]);
  RAM #(.addrWidth(16), .dataWidth(16), .bus("separate")) ram_1 (
    .addr(ALU_out_6), .data(ram_1_data), .str(control_logic_2_main_1_memread[1]), .clk(multiplexer_3_out),
    .ld(control_logic_2_main_1_memread[0]), .clr(RESET));  // open: din, sel
  Multiplexer #(.select(2), .width(16), .enable("false")) multiplexer_8 (
    .in0(ALU_out_6), .in1(ram_1_data), .in2(ALU_max), .in3(ALU_min), .out(multiplexer_8_out),
    .sel(control_logic_2_main_1_memtoreg));

  // Notes on the sheet:
  //   contents of rom_1 (hex, n*v repeats v):
  //   4 408 828 411 c8fe 6003 12*0 1
endmodule
